// Logisim project cpuproject.circ as structural Verilog
module ULA (
  input  [15:0] A,
  input  [3:0] OP,
  input  [15:0] B,
  output [15:0] R,
  output R1
);

  wire BigOut, EquOut;
  wire [15:0] AndOut, DivOut, MulOut, NotOut, OrOut, ShLOut, ShROut, SubOut, SumOut;

  Adder #(.width(16)) adder_1 (.a(A), .b(B), .out(SumOut));  // open: cin, cout
  Subtractor #(.width(16)) subtractor_1 (.a(A), .b(B), .out(SubOut));  // open: bin, bout
  Multiplier #(.width(16)) multiplier_1 (.a(A), .b(B), .out(MulOut));  // open: cin, cout
  Divider #(.width(16)) divider_1 (.a(A), .b(B), .out(DivOut));  // open: upper, rem
  Comparator #(.width(16)) comparator_1 (.a(A), .b(B), .gt(BigOut), .eq(EquOut));  // open: lt
  assign NotOut = ~A;  // NOT_Gate not_1, 16 bits wide
  assign AndOut = A & B;  // AND_Gate and_1, 16 bits wide
  assign OrOut = A | B;  // OR_Gate or_1, 16 bits wide
  Shifter #(.width(16)) shifter_1 (.in(A), .\dist (B[3:0]), .out(ShLOut));
  Shifter #(.width(16), .shift("lr")) shifter_2 (.in(A), .\dist (B[3:0]), .out(ShROut));
endmodule

module XOR (
  input  in_1,
  input  in_2,
  output out_3
);

  wire and_1_out, and_2_out, not_1_out, not_2_out;

  not not_1 (not_1_out, in_1);
  not not_2 (not_2_out, in_2);
  and and_1 (and_1_out, not_1_out, in_2);
  and and_2 (and_2_out, in_1, not_2_out);
  or or_1 (out_3, and_1_out, and_2_out);
endmodule

module SOMA1 (
  input  in_1,
  input  in_2,
  output out_3,
  output out_4
);

  and and_1 (out_3, in_1, in_2);
  XOR xor_1 (.in_1(in_1), .in_2(in_2), .out_3(out_4));
endmodule

module SOMA3 (
  input  [2:0] in_1,
  input  [2:0] in_2,
  output out_3,
  output [2:0] out_4
);

  wire soma1_1_out_3, soma1_2_out_3, soma1_2_out_4, soma1_3_out_3, soma1_4_out_3, soma1_4_out_4,
       soma1_5_out_3, soma1_5_out_4, soma1_6_out_3;

  SOMA1 soma1_1 (.in_1(in_1[0]), .in_2(in_2[0]), .out_3(soma1_1_out_3), .out_4(out_4[0]));
  SOMA1 soma1_2 (.in_1(in_1[1]), .in_2(in_2[1]), .out_3(soma1_2_out_3), .out_4(soma1_2_out_4));
  SOMA1 soma1_3 (.in_1(soma1_2_out_4), .in_2(soma1_1_out_3), .out_3(soma1_3_out_3), .out_4(out_4[1]));
  SOMA1 soma1_4 (.in_1(in_1[2]), .in_2(in_2[2]), .out_3(soma1_4_out_3), .out_4(soma1_4_out_4));
  SOMA1 soma1_5 (.in_1(soma1_2_out_3), .in_2(soma1_3_out_3), .out_3(soma1_5_out_3), .out_4(soma1_5_out_4));
  SOMA1 soma1_6 (.in_1(soma1_4_out_4), .in_2(soma1_5_out_4), .out_3(soma1_6_out_3), .out_4(out_4[2]));
  or or_1 (out_3, soma1_4_out_3, soma1_6_out_3, soma1_5_out_3);
endmodule

module Mux (
  input  in_1,
  input  in_2,
  input  in_3
);
endmodule
